# Fritzing sketch timer_example (saved by Fritzing 0.9.6b)
breadboards: 1

parts:
  R1 = Resistor [tolerance=±5% resistance=10k package="0805 [SMD]"]
  Part1 = Arduino Nano (Rev3.0) (ICSP)
  S1 = Pushbutton [package="[THT]"]

nets:
  N1: R1.Pin_0, Part1.D2, S1.Pin_3, S1.Pin_4
  N2: R1.Pin_1, Part1.GND
  N3: Part1.D4, S1.Pin_1, S1.Pin_2
